// Logisim project Exer_FlipFlops.circ as structural Verilog: 1 circuit, main circuit main
module main (
  input  in_1,
  input  in_2,
  input  in_3,
  input  in_4,
  input  in_5,
  input  in_6,
  input  in_7,
  input  in_8,
  input  in_9,
  input  in_10,
  input  in_11,
  input  in_12,
  input  in_13,
  output out_14,
  output out_15,
  output out_16,
  output out_17
);

  wire clock_1_out, clock_2_out, clock_3_out;

  Clock clock_1 (.out(clock_1_out));
  S_R_Flip_Flop s_r_ff_1 (.S(in_8), .clk(clock_1_out), .R(in_10), .Q(out_16));  // open: Qn, preset, reset, en
  Clock clock_2 (.out(clock_2_out));
  Clock clock_3 (.out(clock_3_out));
  D_Flip_Flop d_ff_1 (.clk(in_1), .D(in_2), .Q(out_14), .preset(in_3), .reset(in_4));  // open: Qn, en
  T_Flip_Flop t_ff_1 (.clk(clock_2_out), .T(in_5), .Q(out_15), .preset(in_6), .reset(in_7));  // open: Qn, en
  J_K_Flip_Flop j_k_ff_1 (
    .J(in_9), .clk(clock_3_out), .K(in_11), .Q(out_17), .preset(in_12), .reset(in_13));  // open: Qn, en
endmodule
